// Digital circuit Lobinho.dig as structural Verilog
module Lobinho (
  input  clk,
  output [4:0] out_1,
  output [4:0] out_2,
  output [9:0] out_3,
  output [1:0] out_5,
  output [2:0] out_6
);

  wire button_1_out, button_2_out, button_3_out, button_4_out;

  Button button_1 (.out(button_1_out));
  Button button_2 (.out(button_2_out));
  Button button_3 (.out(button_3_out));
  Button button_4 (.out(button_4_out));
  PoliLobinho #(.applicationType("IVERILOG"), .CodeFile("C:\\Users\\anton\\Documents\\PoliLobinho\\digital.v")) u_PoliLobinho (
    .clock(clk), .botao(button_1_out), .reset(button_2_out), .jogar(button_3_out), .passa(button_4_out),
    .db_estado(out_1), .db_seed(out_2), .jogador_atual(out_6), .classe_atual(out_5), .jogo_atual(out_3));

  // Notes on the sheet:
  //   clk: Hz: 1000
endmodule
